// Logisim project DigitalClockAlarm.circ as structural Verilog: 1 circuit, main circuit main
module main (
  input  [3:0] in_1,
  input  [3:0] in_2,
  input  [3:0] in_3,
  input  [3:0] in_4
);

  wire and_1_out, and_2_out, and_3_out, and_4_out, and_5_out, and_6_out, and_7_out, and_8_out, and_10_out,
       and_11_out, and_12_out, and_13_out, and_14_out, and_15_out, and_16_out, and_17_out, and_18_out,
       and_19_out, and_21_out, and_22_out, and_23_out, and_24_out, and_25_out, and_27_out, and_28_out,
       and_29_out, and_31_out, and_32_out, and_33_out, and_34_out, and_35_out, and_36_out, and_37_out,
       and_38_out, BTNC_q, button_1_out, button_2_out, button_3_out, button_4_out, button_5_out, clock_1_out,
       comparator_1_eq, comparator_2_eq, comparator_3_eq, comparator_4_eq, counter_11_q, d_ff_1_q, d_ff_2_q,
       decoder_1_out0, decoder_1_out1, decoder_1_out2, decoder_1_out3, multiplexer_1_out, multiplexer_2_out,
       multiplexer_3_out, multiplexer_4_out, multiplexer_6_out, multiplexer_7_out, multiplexer_8_out,
       multiplexer_10_out, multiplexer_11_out, multiplexer_12_out, multiplexer_13_out, multiplexer_15_out,
       multiplexer_16_out, multiplexer_17_out, multiplexer_19_out, multiplexer_20_out, nor_1_out, nor_2_out,
       nor_3_out, nor_5_out, nor_6_out, not_1_out, not_2_out, not_3_out, not_4_out, not_5_out, not_6_out,
       not_7_out, not_8_out, not_9_out, not_10_out, not_11_out, not_12_out, or_1_out, or_2_out, or_3_out,
       or_4_out, or_5_out, or_6_out, or_7_out, or_8_out, or_9_out, or_10_out, or_11_out, or_12_out;
  wire [1:0] and_26_out, counter_1_q, counter_2_q, counter_10_q, multiplexer_5_out, nor_4_out;
  wire [1:1] and_9_out;
  wire [2:0] counter_5_q, counter_6_q, multiplexer_14_out;
  wire [3:0] bcd_to_7_segment_decoder_3_p1, bcd_to_7_segment_decoder_8_p1, counter_3_q, counter_4_q,
       counter_7_q, multiplexer_18_out;
  wire [5:0] counter_8_q;

  not not_1 (not_1_out, multiplexer_20_out);
  or or_1 (or_1_out, not_1_out, decoder_1_out0, decoder_1_out1);
  not not_2 (not_2_out, or_1_out);
  Multiplexer #(.select(2)) multiplexer_1 (
    .in0(and_8_out), .in1(or_5_out), .in2(1'b0), .in3(1'b0), .out(multiplexer_1_out),
    .sel({nor_4_out[0], nor_4_out[1]}));
  Clock clock_1 (.out(clock_1_out));
  Multiplexer multiplexer_2 (.in0(1'b1), .in1(and_26_out[0]), .out(multiplexer_2_out), .sel(and_9_out[1]));
  Multiplexer multiplexer_3 (.in0(clock_1_out), .in1(or_10_out), .out(multiplexer_3_out), .sel(and_9_out[1]));
  Multiplexer #(.select(2)) multiplexer_4 (
    .in0(and_5_out), .in1(1'b0), .in2(and_1_out), .in3(and_2_out), .out(multiplexer_4_out),
    .sel({and_9_out[1], and_26_out[0]}));
  and and_1 (and_1_out, button_4_out, not_3_out);
  Counter #(.max('h3), .width(2)) counter_1 (
    .clr(or_3_out), .up(multiplexer_2_out), .count(multiplexer_4_out), .clk(multiplexer_3_out),
    .Q(counter_1_q));  // open: load, D, carry
  and and_2 (and_2_out, button_1_out, and_13_out);
  or or_2 (or_2_out, and_10_out, and_3_out);
  Counter #(.max('h3), .width(2)) counter_2 (
    .clr(or_2_out), .up(nor_4_out[1]), .count(decoder_1_out2), .clk(multiplexer_1_out), .Q(counter_2_q));  // open: load, D, carry
  or or_3 (or_3_out, and_11_out, and_4_out);
  _7_Segment_Display u_7_segment_display_1 ();  // open: g, f, a, b, e, d, c, dp
  // BCD_to_7_Segment_decoder bcd_to_7_segment_decoder_1: pin names not known; wires that end beside it: 1'b0
  _7_Segment_Display u_7_segment_display_2 ();  // open: g, f, a, b, e, d, c, dp
  // BCD_to_7_Segment_decoder bcd_to_7_segment_decoder_2: pin names not known; wires that end beside it: 1'b0
  Multiplexer #(.width(2)) multiplexer_5 (
    .in0(counter_1_q), .in1(counter_2_q), .out(multiplexer_5_out), .sel(not_2_out));
  and and_3 (and_3_out, counter_2_q[0], counter_2_q[1]);
  D_Flip_Flop d_ff_1 (.D(and_16_out), .clk(button_4_out), .Q(d_ff_1_q));  // open: Qn, preset, reset
  or or_4 (or_4_out, counter_1_q[0], counter_1_q[1]);
  and and_4 (and_4_out, counter_1_q[0], counter_1_q[1]);
  and and_5 (and_5_out, and_14_out, and_13_out);
  Multiplexer multiplexer_6 (.in0(1'b1), .in1(and_26_out[0]), .out(multiplexer_6_out), .sel(and_9_out[1]));
  Multiplexer multiplexer_7 (.in0(clock_1_out), .in1(or_10_out), .out(multiplexer_7_out), .sel(and_9_out[1]));
  and and_6 (and_6_out, and_1_out, or_4_out);
  and and_7 (and_7_out, button_4_out, nor_1_out);
  Counter #(.max('hf), .width(4)) counter_3 (
    .clr(or_6_out), .load(and_6_out), .up(multiplexer_6_out), .count(multiplexer_8_out),
    .clk(multiplexer_7_out), .D(in_1), .Q(counter_3_q));  // open: carry
  Multiplexer multiplexer_8 (.in0(and_14_out), .in1(1'b1), .out(multiplexer_8_out), .sel(and_9_out[1]));
  _7_Segment_Display u_7_segment_display_3 ();  // open: g, f, a, b, e, d, c, dp
  // BCD_to_7_Segment_decoder bcd_to_7_segment_decoder_3: pin names not known; wires that end beside it: bcd_to_7_segment_decoder_3_p1
  Multiplexer #(.width(4)) multiplexer_9 (
    .in0(counter_3_q), .in1(counter_4_q), .out(bcd_to_7_segment_decoder_3_p1), .sel(not_2_out));
  Counter #(.max('hf), .width(4)) counter_4 (
    .clr(or_5_out), .load(and_7_out), .up(nor_4_out[1]), .count(decoder_1_out2), .clk(or_9_out), .D(in_4),
    .Q(counter_4_q));  // open: carry
  and and_8 (and_8_out, nor_1_out, not_4_out);
  not not_3 (not_3_out, or_7_out);
  or or_5 (or_5_out, and_10_out, and_15_out);
  not not_4 (not_4_out, d_ff_1_q);
  _7_Segment_Display u_7_segment_display_4 ();  // open: g, f, a, b, e, d, c, dp
  // BCD_to_7_Segment_decoder bcd_to_7_segment_decoder_4: pin names not known; wires that end beside it: counter_4_q
  and and_9 (and_9_out[1], decoder_1_out0, BTNC_q);
  or or_6 (or_6_out, and_11_out, and_12_out);
  or or_7 (or_7_out, counter_3_q[0], counter_3_q[1], counter_3_q[2], counter_3_q[3]);
  and and_10 (and_10_out, counter_2_q[1], counter_4_q[2]);
  nor nor_1 (nor_1_out, counter_4_q[3], counter_4_q[2], counter_4_q[0], counter_4_q[1]);
  and and_11 (and_11_out, counter_1_q[1], counter_3_q[2]);
  and and_12 (and_12_out, counter_3_q[1], counter_3_q[3]);
  and and_13 (and_13_out, counter_3_q[0], counter_3_q[3]);
  and and_14 (and_14_out, and_22_out, and_21_out);
  and and_15 (and_15_out, counter_4_q[1], counter_4_q[3]);
  nor nor_2 (nor_2_out, counter_4_q[2], counter_4_q[3], counter_4_q[2]);
  Multiplexer #(.select(2)) multiplexer_10 (
    .in0(and_22_out), .in1(1'b0), .in2(and_24_out), .in3(and_17_out), .out(multiplexer_10_out),
    .sel(and_26_out));
  and and_16 (and_16_out, counter_4_q[0], nor_2_out);
  Multiplexer #(.select(2)) multiplexer_11 (
    .in0(and_19_out), .in1(1'b0), .in2(and_35_out), .in3(1'b0), .out(multiplexer_11_out), .sel(nor_4_out));
  Multiplexer multiplexer_12 (.in0(clock_1_out), .in1(or_10_out), .out(multiplexer_12_out), .sel(and_26_out[1]));
  Counter #(.max('h7), .width(3)) counter_5 (
    .clr(and_23_out), .up(multiplexer_13_out), .count(multiplexer_10_out), .clk(multiplexer_12_out),
    .Q(counter_5_q));  // open: load, D, carry
  and and_17 (and_17_out, button_1_out, and_28_out);
  Multiplexer multiplexer_13 (.in0(1'b1), .in1(and_26_out[0]), .out(multiplexer_13_out), .sel(and_26_out[1]));
  and and_18 (and_18_out, or_8_out, and_24_out);
  _7_Segment_Display u_7_segment_display_5 ();  // open: g, f, a, b, e, d, c, dp
  // BCD_to_7_Segment_decoder bcd_to_7_segment_decoder_5: pin names not known; wires that end beside it: 1'b0
  Counter #(.max('h7), .width(3)) counter_6 (
    .clr(and_25_out), .up(nor_4_out[1]), .count(decoder_1_out3), .clk(multiplexer_11_out), .Q(counter_6_q));  // open: load, D, carry
  and and_19 (and_19_out, nor_5_out, not_5_out);
  not not_5 (not_5_out, d_ff_2_q);
  LED led_1 (.in(decoder_1_out0));
  and and_20 (and_26_out[1], decoder_1_out1, BTNC_q);
  Multiplexer #(.width(3)) multiplexer_14 (
    .in0(counter_5_q), .in1(counter_6_q), .out(multiplexer_14_out), .sel(not_2_out));
  _7_Segment_Display u_7_segment_display_6 ();  // open: g, f, a, b, e, d, c, dp
  // BCD_to_7_Segment_decoder bcd_to_7_segment_decoder_6: pin names not known
  LED led_2 (.in(decoder_1_out1));
  LED led_3 (.in(decoder_1_out2));
  and and_21 (and_21_out, counter_5_q[0], counter_5_q[2]);
  or or_8 (or_8_out, counter_5_q[2], counter_5_q[0], counter_5_q[1]);
  LED led_4 (.in(decoder_1_out3));
  and and_22 (and_22_out, and_34_out, and_28_out);
  and and_23 (and_23_out, counter_5_q[1], counter_5_q[2]);
  Multiplexer multiplexer_15 (.in0(and_34_out), .in1(1'b1), .out(multiplexer_15_out), .sel(and_26_out[1]));
  Multiplexer multiplexer_16 (.in0(1'b1), .in1(and_26_out[0]), .out(multiplexer_16_out), .sel(and_26_out[1]));
  Counter #(.max('hf), .width(4)) counter_7 (
    .clr(and_27_out), .load(and_18_out), .up(multiplexer_16_out), .count(multiplexer_15_out),
    .clk(multiplexer_17_out), .D(in_2), .Q(counter_7_q));  // open: carry
  and and_24 (and_24_out, nor_3_out, button_4_out);
  and and_25 (and_25_out, counter_6_q[1], counter_6_q[2]);
  Decoder #(.select(2)) decoder_1 (
    .out0(decoder_1_out0), .out1(decoder_1_out1), .out2(decoder_1_out2), .out3(decoder_1_out3),
    .sel(counter_10_q));  // open: en
  Multiplexer multiplexer_17 (.in0(clock_1_out), .in1(or_10_out), .out(multiplexer_17_out), .sel(and_26_out[1]));
  nor nor_3 (nor_3_out, counter_7_q[0], counter_7_q[1], counter_7_q[2], counter_7_q[3]);
  Multiplexer #(.width(4)) multiplexer_18 (
    .in0(counter_7_q), .in1(bcd_to_7_segment_decoder_8_p1), .out(multiplexer_18_out), .sel(not_2_out));
  _7_Segment_Display u_7_segment_display_7 ();  // open: g, f, a, b, e, d, c, dp
  // BCD_to_7_Segment_decoder bcd_to_7_segment_decoder_7: pin names not known; wires that end beside it: multiplexer_18_out
  nor nor_4 (nor_4_out[0], button_4_out, button_1_out);
  or or_9 (or_9_out, button_1_out, button_4_out);
  and and_26 (and_26_out[0], button_1_out, not_6_out);
  not not_6 (not_6_out, button_4_out);
  or or_10 (or_10_out, button_1_out, button_4_out);
  LED led_5 (.in(multiplexer_20_out));
  and and_27 (and_27_out, counter_7_q[1], counter_7_q[3]);
  and and_28 (and_28_out, counter_7_q[0], counter_7_q[3]);
  not not_7 (not_7_out, button_4_out);
  not not_8 (not_8_out, BTNC_q);
  Counter #(.max('h3f), .width(6)) counter_8 (
    .clr(and_33_out), .clk(and_29_out), .Q(counter_8_q));  // open: load, up, count, D, carry
  and and_29 (and_29_out, not_8_out, clock_1_out);
  _7_Segment_Display u_7_segment_display_8 (.dp(and_29_out));  // open: g, f, a, b, e, d, c
  and and_30 (nor_4_out[1], button_1_out, not_7_out);
  D_Flip_Flop d_ff_2 (.D(and_36_out), .clk(button_4_out), .Q(d_ff_2_q));  // open: Qn, preset, reset
  _7_Segment_Display u_7_segment_display_9 ();  // open: g, f, a, b, e, d, c, dp
  // BCD_to_7_Segment_decoder bcd_to_7_segment_decoder_8: pin names not known; wires that end beside it: bcd_to_7_segment_decoder_8_p1
  Button button_1 (.out(button_1_out));
  Button button_2 (.out(button_2_out));
  Button button_3 (.out(button_3_out));
  Button button_4 (.out(button_4_out));
  not not_9 (not_9_out, counter_11_q);
  and and_31 (and_31_out, button_4_out, nor_5_out);
  Button button_5 (.out(button_5_out));
  Counter #(.max('h1), .width(1)) BTNC (
    .count(not_9_out), .clk(button_3_out), .Q(BTNC_q));  // open: clr, load, up, D, carry
  Counter #(.max('hf), .width(4)) counter_9 (
    .clr(and_35_out), .load(and_31_out), .up(nor_4_out[1]), .count(decoder_1_out3), .clk(or_9_out), .D(in_3),
    .Q(bcd_to_7_segment_decoder_8_p1));  // open: carry
  not not_10 (not_10_out, BTNC_q);
  not not_11 (not_11_out, button_2_out);
  and and_32 (and_32_out, not_11_out, button_5_out);
  or or_11 (or_11_out, button_2_out, button_5_out);
  and and_33 (and_33_out, counter_8_q[2], counter_8_q[3], counter_8_q[4], counter_8_q[5]);
  and and_34 (and_34_out, counter_8_q[0], counter_8_q[1], counter_8_q[3], counter_8_q[4], counter_8_q[5]);
  nor nor_5 (nor_5_out, bcd_to_7_segment_decoder_8_p1[3], bcd_to_7_segment_decoder_8_p1[2], bcd_to_7_segment_decoder_8_p1[0], bcd_to_7_segment_decoder_8_p1[1]);
  Counter #(.max('h3), .width(2)) counter_10 (
    .clr(not_10_out), .up(and_32_out), .count(BTNC_q), .clk(or_11_out), .Q(counter_10_q));  // open: load, D, carry
  and and_35 (and_35_out, bcd_to_7_segment_decoder_8_p1[1], bcd_to_7_segment_decoder_8_p1[3]);
  nor nor_6 (nor_6_out, bcd_to_7_segment_decoder_8_p1[1], bcd_to_7_segment_decoder_8_p1[2], bcd_to_7_segment_decoder_8_p1[3]);
  and and_36 (and_36_out, bcd_to_7_segment_decoder_8_p1[0], nor_6_out);
  and and_37 (and_37_out, and_38_out, not_12_out);
  Multiplexer multiplexer_19 (.in0(and_37_out), .in1(or_12_out), .out(multiplexer_19_out), .sel(counter_11_q));
  or or_12 (or_12_out, button_2_out, button_4_out, button_3_out, button_5_out, button_1_out);
  Counter #(.max('h1), .width(1)) counter_11 (
    .clk(multiplexer_19_out), .Q(counter_11_q));  // open: clr, load, up, count, D, carry
  not not_12 (not_12_out, or_12_out);
  Comparator #(.width(4)) comparator_1 (
    .a(counter_7_q), .b(bcd_to_7_segment_decoder_8_p1), .eq(comparator_1_eq));  // open: gt, lt
  Comparator #(.width(3)) comparator_2 (.a(counter_5_q), .b(counter_6_q), .eq(comparator_2_eq));  // open: gt, lt
  Comparator #(.width(4)) comparator_3 (.a(counter_3_q), .b(counter_4_q), .eq(comparator_3_eq));  // open: gt, lt
  Comparator #(.width(2)) comparator_4 (.a(counter_1_q), .b(counter_2_q), .eq(comparator_4_eq));  // open: gt, lt
  Multiplexer multiplexer_20 (.in0(BTNC_q), .in1(clock_1_out), .out(multiplexer_20_out), .sel(counter_11_q));
  and and_38 (and_38_out, comparator_1_eq, comparator_2_eq, comparator_3_eq, comparator_4_eq);

  // Notes on the sheet:
  //   in_1: initial=0x9
  //   in_4: initial=0x9
  //   in_2: initial=0x9
  //   in_3: initial=0x9
  //   and
  //   or
endmodule
